# Fritzing sketch esp_pract (saved by Fritzing 0.9.4)
breadboards: 1

parts:
  U1 = NodeMCU V1.0
  S1 = KY-026

nets:
  N1: U1.3V3, S1.pin3
  N2: U1.GND, S1.pin2
  N3: U1.A0, S1.pin1

custom parts:
  NodeMCU V1.0: ESP8266 based NodeMCU
  KY-026: ky-026 flame sensor module
